// Logisim project proyecto.circ as structural Verilog: 6 circuits, main circuit Main
module Main (
  output out_1,
  output out_2
);

  wire and_1_out, and_2_out, and_3_out, and_4_out, and_5_out, and_6_out, and_7_out, clock_1_out, clock_2_out,
       clock_3_out, comparator_1_eq, comparator_1_gt, comparator_1_lt, comparator_2_eq, comparator_3_eq,
       comparator_4_eq, comparator_4_lt, comparator_5_eq, comparator_5_lt, comparator_6_eq, comparator_6_lt,
       comparator_7_eq, comparator_7_lt, ContCPU, ContJug, CPU__21, decoder_1_out0, decoder_1_out1,
       decoder_1_out2, decoder_2_out0, decoder_2_out1, decoder_2_out2, Detenerse, DetenerseCPU, Final,
       Iniciar, Jug_21, JugParo, multiplexer_3_out, multiplexer_4_out, or_1_out, or_3_out, or_5_out,
       or_6_out, or_7_out, or_8_out, or_9_out, Pedir, register_1_q, verificar_resultado_1_out_3,
       verificar_resultado_1_out_4, verificar_suma_1_out_6, verificar_suma_1_out_7;
  wire [1:0] bit_extender_4_out, bit_extender_5_out, counter_1_q, counter_2_q, multiplexer_7_out,
       multiplexer_8_out, random_1_out;
  wire [3:0] Carta1PC, Carta2PC, Carta3PC, Carta4PC, Carta5PC, Carta_1, Carta_2, Carta_3, Carta_4, Carta_5,
       \comprobar_número_cpu_1_out_2 , \comprobar_número_cpu_2_out_2 , \comprobar_número_cpu_3_out_2 ,
       \comprobar_número_jugador_1_out_2 , \comprobar_número_jugador_2_out_2 ,
       \comprobar_número_jugador_3_out_2 , Digito1PC, Digito2PC, Digito_1, Digito_2, entregar_cartas_1_out_2,
       entregar_cartas_1_out_3, entregar_cartas_1_out_4, entregar_cartas_1_out_5, verificar_suma_1_out_9;
  wire [4:0] bit_extender_2_out, bit_extender_3_out, multiplexer_1_out, multiplexer_2_out, multiplexer_5_out,
       multiplexer_6_out, NumDetener, subtractor_1_out, subtractor_2_out, subtractor_3_out, subtractor_4_out,
       subtractor_5_out, verificar_suma_2_out_9;
  wire [4:4] verificar_suma_1_out_9_2;

  Hex_Digit_Display hex_digit_display_1 (.value(Carta_1));  // open: dp
  Hex_Digit_Display hex_digit_display_2 (.value(Carta_2));  // open: dp
  Hex_Digit_Display hex_digit_display_3 (.value(Carta1PC));  // open: dp
  or or_1 (or_1_out, ~ContJug, or_3_out);  // OR_Gate
  Clock clock_1 (.out(clock_1_out));
  Register #(.width(1), .Select("low")) register_1 (
    .D(Final), .Q(register_1_q), .clk(Final), .clr(Iniciar));  // open: en
  Hex_Digit_Display hex_digit_display_4 (.value(Carta_3));  // open: dp
  Hex_Digit_Display hex_digit_display_5 (.value(Carta2PC));  // open: dp
  Hex_Digit_Display hex_digit_display_6 (.value(Carta3PC));  // open: dp
  and and_1 (and_1_out, or_1_out, clock_1_out);
  Random #(.width(2), .trigger("falling")) random_1 (
    .clk(clock_1_out), .next(and_2_out), .out(random_1_out));  // open: clr
  and and_2 (and_2_out, clock_1_out, ~DetenerseCPU, register_1_q);  // AND_Gate
  Hex_Digit_Display hex_digit_display_7 (.value(Carta_4));  // open: dp
  Hex_Digit_Display hex_digit_display_8 (.value(Carta4PC));  // open: dp
  assign NumDetener = {{3{1'b0}}, random_1_out};  // Bit_Extender bit_extender_1
  Subtractor #(.width(5)) subtractor_1 (.a(5'b10101), .b(NumDetener), .out(subtractor_1_out));  // open: bin, bout
  Button button_1 (.out(Iniciar));
  Hex_Digit_Display hex_digit_display_9 (.value(Carta_5));  // open: dp
  Button button_2 (.out(Pedir));
  Button button_3 (.out(Detenerse));
  Hex_Digit_Display hex_digit_display_10 (.value(Carta5PC));  // open: dp
  Comparator #(.width(5), .mode("unsigned")) comparator_1 (
    .a(subtractor_1_out), .b({verificar_suma_1_out_9_2[4], verificar_suma_1_out_9}), .gt(comparator_1_gt),
    .eq(comparator_1_eq), .lt(comparator_1_lt));
  Entregar_cartas entregar_cartas_1 (
    .in_1(Iniciar), .out_2(entregar_cartas_1_out_2), .out_3(entregar_cartas_1_out_3),
    .out_4(entregar_cartas_1_out_4), .out_5(entregar_cartas_1_out_5));
  or or_2 (DetenerseCPU, comparator_1_eq, comparator_1_lt, ~ContCPU);  // OR_Gate
  Register #(.width(1), .Select("low")) register_2 (
    .D(Detenerse), .Q(JugParo), .clk(Detenerse), .clr(Iniciar));  // open: en
  and and_3 (and_3_out, comparator_1_gt, ~CPU__21);  // AND_Gate
  and and_4 (and_4_out, ~Jug_21, ~JugParo, Pedir);  // AND_Gate
  or or_3 (or_3_out, Pedir, JugParo);
  Counter #(.width(2), .max('h3), .trigger("falling")) counter_1 (
    .count(ContCPU), .Q(counter_1_q), .clk(and_5_out), .clr(Iniciar));  // open: load, D, carry, preset, down
  and and_5 (and_5_out, and_1_out, and_3_out);
  Hex_Digit_Display hex_digit_display_11 (.value(Digito_1));  // open: dp
  Hex_Digit_Display hex_digit_display_12 (.value(Digito1PC));  // open: dp
  Counter #(.width(2), .max('h3), .trigger("falling")) counter_2 (
    .count(ContJug), .Q(counter_2_q), .clk(and_4_out), .clr(Iniciar));  // open: load, D, carry, preset, down
  Decoder #(.select(2), .enable("false")) decoder_1 (
    .out0(decoder_1_out0), .out1(decoder_1_out1), .out2(decoder_1_out2), .sel(counter_2_q));  // open: out3
  Decoder #(.select(2), .enable("false")) decoder_2 (
    .out0(decoder_2_out0), .out1(decoder_2_out1), .out2(decoder_2_out2), .sel(counter_1_q));  // open: out3
  Hex_Digit_Display hex_digit_display_13 (.value(Digito_2));  // open: dp
  Hex_Digit_Display hex_digit_display_14 (.value(Digito2PC));  // open: dp
  Comparator #(.width(2), .mode("unsigned")) comparator_2 (
    .a(counter_2_q), .b(2'b11), .eq(comparator_2_eq));  // open: gt, lt
  not not_1 (ContCPU, comparator_3_eq);
  Comparator #(.width(2), .mode("unsigned")) comparator_3 (
    .a(counter_1_q), .b(2'b11), .eq(comparator_3_eq));  // open: gt, lt
  not not_2 (ContJug, comparator_2_eq);
  \Comprobar_número_Jugador  \comprobar_número_jugador_1  (
    .in_1(and_4_out), .out_2(\comprobar_número_jugador_1_out_2 ));
  \Comprobar_número_Jugador  \comprobar_número_jugador_2  (
    .in_1(and_4_out), .out_2(\comprobar_número_jugador_2_out_2 ));
  \Comprobar_número_Jugador  \comprobar_número_jugador_3  (
    .in_1(and_4_out), .out_2(\comprobar_número_jugador_3_out_2 ));
  \Comprobar_número_CPU  \comprobar_número_cpu_1  (.in_1(and_5_out), .out_2(\comprobar_número_cpu_1_out_2 ));
  \Comprobar_número_CPU  \comprobar_número_cpu_2  (.in_1(and_5_out), .out_2(\comprobar_número_cpu_2_out_2 ));
  \Comprobar_número_CPU  \comprobar_número_cpu_3  (.in_1(and_5_out), .out_2(\comprobar_número_cpu_3_out_2 ));
  Register #(.width(4), .trigger("falling"), .Select("low")) Carta1 (
    .D(entregar_cartas_1_out_2), .Q(Carta_1), .clk(Iniciar));  // open: en, clr
  Register #(.width(4), .trigger("falling"), .Select("low")) Carta2 (
    .D(entregar_cartas_1_out_3), .Q(Carta_2), .clk(Iniciar));  // open: en, clr
  Register #(.width(4), .trigger("falling"), .Select("low")) CartaTemp3 (
    .D(\comprobar_número_jugador_1_out_2 ), .Q(Carta_3), .clk(decoder_1_out0), .clr(Iniciar));  // open: en
  Register #(.width(4), .trigger("falling"), .Select("low")) CartaTemp4 (
    .D(\comprobar_número_jugador_2_out_2 ), .Q(Carta_4), .clk(decoder_1_out1), .clr(Iniciar));  // open: en
  Register #(.width(4), .trigger("falling"), .Select("low")) CartaTemp5 (
    .D(\comprobar_número_jugador_3_out_2 ), .Q(Carta_5), .clk(decoder_1_out2), .clr(Iniciar));  // open: en
  Register #(.width(4), .trigger("falling"), .Select("low")) Carta1Cpu (
    .D(entregar_cartas_1_out_4), .Q(Carta1PC), .clk(Iniciar));  // open: en, clr
  Register #(.width(4), .trigger("falling"), .Select("low")) Carta2Cpu (
    .D(entregar_cartas_1_out_5), .Q(Carta2PC), .clk(Iniciar));  // open: en, clr
  Register #(.width(4), .trigger("falling"), .Select("low")) Carta3Cpu (
    .D(\comprobar_número_cpu_1_out_2 ), .Q(Carta3PC), .clk(decoder_2_out0), .clr(Iniciar));  // open: en
  Register #(.width(4), .trigger("falling"), .Select("low")) Carta4Cpu (
    .D(\comprobar_número_cpu_2_out_2 ), .Q(Carta4PC), .clk(decoder_2_out1), .clr(Iniciar));  // open: en
  Register #(.width(4), .trigger("falling"), .Select("low")) CartaCpu5 (
    .D(\comprobar_número_cpu_3_out_2 ), .Q(Carta5PC), .clk(decoder_2_out2), .clr(Iniciar));  // open: en
  Verificar_Suma verificar_suma_1 (
    .Carta_1(Carta1PC), .Carta_2(Carta2PC), .out_6(verificar_suma_1_out_6), .out_7(verificar_suma_1_out_7),
    .out_9({verificar_suma_1_out_9_2[4], verificar_suma_1_out_9}), .Carta_3(Carta3PC), .Carta_4(Carta4PC),
    .Carta_5(Carta5PC));  // open: out_8
  Verificar_Suma verificar_suma_2 (
    .Carta_1(Carta_1), .Carta_2(Carta_2), .out_6(Jug_21), .out_9(verificar_suma_2_out_9), .Carta_3(Carta_3),
    .Carta_4(Carta_4), .Carta_5(Carta_5));  // open: out_7, out_8
  or or_4 (CPU__21, verificar_suma_1_out_6, verificar_suma_1_out_7);
  Verificar_Resultado verificar_resultado_1 (
    .Suma_cartas_J(verificar_suma_2_out_9),
    .Suma_cartas_M({verificar_suma_1_out_9_2[4], verificar_suma_1_out_9}),
    .out_3(verificar_resultado_1_out_3), .out_4(verificar_resultado_1_out_4));
  Register #(.width(1), .Select("low")) register_3 (
    .D(verificar_resultado_1_out_3), .en(Final), .Q(out_1), .clk(clock_2_out), .clr(Iniciar));
  Clock clock_2 (.out(clock_2_out));
  Register #(.width(1), .Select("low")) register_4 (
    .D(verificar_resultado_1_out_4), .en(Final), .Q(out_2), .clk(clock_3_out), .clr(Iniciar));
  Clock clock_3 (.out(clock_3_out));
  assign bit_extender_2_out = {{1{1'b0}}, verificar_suma_2_out_9[3:0]};  // Bit_Extender bit_extender_2
  Subtractor #(.width(5)) subtractor_2 (
    .a(verificar_suma_2_out_9), .b(5'b01010), .out(subtractor_2_out));  // open: bin, bout
  Comparator #(.width(5), .mode("unsigned")) comparator_4 (
    .a(5'b01010), .b(verificar_suma_2_out_9), .eq(comparator_4_eq), .lt(comparator_4_lt));  // open: gt
  assign bit_extender_3_out = {{1{1'b0}}, verificar_suma_1_out_9};  // Bit_Extender bit_extender_3
  Subtractor #(.width(5)) subtractor_3 (
    .a({verificar_suma_1_out_9_2[4], verificar_suma_1_out_9}), .b(5'b01010), .out(subtractor_3_out));  // open: bin, bout
  Comparator #(.width(5), .mode("unsigned")) comparator_5 (
    .a(5'b01010), .b({verificar_suma_1_out_9_2[4], verificar_suma_1_out_9}), .eq(comparator_5_eq),
    .lt(comparator_5_lt));  // open: gt
  Multiplexer #(.width(5), .enable("false")) multiplexer_1 (
    .in0(bit_extender_2_out), .in1(subtractor_2_out), .out(multiplexer_1_out), .sel(or_5_out));
  or or_5 (or_5_out, comparator_4_eq, comparator_4_lt);
  Multiplexer #(.width(5), .enable("false")) multiplexer_2 (
    .in0(bit_extender_3_out), .in1(subtractor_3_out), .out(multiplexer_2_out), .sel(or_6_out));
  or or_6 (or_6_out, comparator_5_eq, comparator_5_lt);
  Multiplexer #(.enable("false")) multiplexer_3 (.in0(1'b0), .in1(1'b1), .out(multiplexer_3_out), .sel(or_5_out));
  Multiplexer #(.enable("false")) multiplexer_4 (.in0(1'b0), .in1(1'b1), .out(multiplexer_4_out), .sel(or_6_out));
  Subtractor #(.width(5)) subtractor_4 (
    .a(multiplexer_1_out), .b(5'b01010), .out(subtractor_4_out));  // open: bin, bout
  assign bit_extender_4_out = {{1{1'b0}}, multiplexer_3_out};  // Bit_Extender bit_extender_4
  Comparator #(.width(5), .mode("unsigned")) comparator_6 (
    .a(5'b10100), .b(verificar_suma_2_out_9), .eq(comparator_6_eq), .lt(comparator_6_lt));  // open: gt
  or or_7 (or_7_out, comparator_6_eq, comparator_6_lt);
  and and_6 (and_6_out, ~ContJug, ~ContCPU);  // AND_Gate
  and and_7 (and_7_out, JugParo, DetenerseCPU);
  or or_8 (or_8_out, CPU__21, Jug_21);
  Subtractor #(.width(5)) subtractor_5 (
    .a(multiplexer_2_out), .b(5'b01010), .out(subtractor_5_out));  // open: bin, bout
  assign bit_extender_5_out = {{1{1'b0}}, multiplexer_4_out};  // Bit_Extender bit_extender_5
  or or_9 (or_9_out, comparator_7_eq, comparator_7_lt);
  Comparator #(.width(5), .mode("unsigned")) comparator_7 (
    .a(5'b10100), .b({verificar_suma_1_out_9_2[4], verificar_suma_1_out_9}), .eq(comparator_7_eq),
    .lt(comparator_7_lt));  // open: gt
  Multiplexer #(.width(5), .enable("false")) multiplexer_5 (
    .in0(multiplexer_1_out), .in1(subtractor_4_out), .out(multiplexer_5_out), .sel(or_7_out));
  or or_10 (Final, and_6_out, and_7_out, or_8_out);
  Multiplexer #(.width(5), .enable("false")) multiplexer_6 (
    .in0(multiplexer_2_out), .in1(subtractor_5_out), .out(multiplexer_6_out), .sel(or_9_out));
  Bit_Extender #(.in_width(5), .out_width(4), .\type ("zero")) bit_extender_6 (.in(multiplexer_5_out), .out(Digito_2));
  assign Digito_1 = {{2{1'b0}}, multiplexer_7_out};  // Bit_Extender bit_extender_7
  Multiplexer #(.width(2), .enable("false")) multiplexer_7 (
    .in0(bit_extender_4_out), .in1(2'b10), .out(multiplexer_7_out), .sel(or_7_out));
  Bit_Extender #(.in_width(5), .out_width(4), .\type ("zero")) bit_extender_8 (.in(multiplexer_6_out), .out(Digito2PC));
  assign Digito1PC = {{2{1'b0}}, multiplexer_8_out};  // Bit_Extender bit_extender_9
  Multiplexer #(.width(2), .enable("false")) multiplexer_8 (
    .in0(bit_extender_5_out), .in1(2'b10), .out(multiplexer_8_out), .sel(or_9_out));

  // Other names for the same wires on the sheet: Gano = out_1; Perdio = out_2

  // Notes on the sheet:
  //   Sus cartas son:
  //   Las cartas del CPU son:
  //   Para iniciar el juego, presione el botón:
  //   Si desea otra carta, presion el botón:
  //   Bienvenid@ a 21!
  //   Resultado
  //   Instrucciones:
  //   Si se enciende el de la izquierda, ganó! :) $Si se enciende el de la derecha, perdió :(
  //   La suma de cartas del CPU es:
  //   La suma de sus cartas actualmente es:
  //   -Para comenzar a jugar, debe presionar el boton de iniciar juego$
  //   -La idea del juego es acercarse lo mayor posible al numero 21
  //   -Estará jugando contra un segundo jugador, el cual es manejado por el computador
  //   -En caso de sobrepasar el 21, aparecera un 00, lo cual significa una derrota
  //   -En caso de que quiera mas cartas (máximo 3 cartas extra), ademas de las 2 iniciales, presione el boton de pedir carta
endmodule

module Verificar_Resultado (
  input  [4:0] Suma_cartas_J,
  input  [4:0] Suma_cartas_M,
  output out_3,
  output out_4
);

  wire comparator_1_eq, comparator_1_lt;

  Comparator #(.width(5), .mode("unsigned")) comparator_1 (
    .a(Suma_cartas_J), .b(Suma_cartas_M), .gt(out_3), .eq(comparator_1_eq), .lt(comparator_1_lt));
  or or_1 (out_4, comparator_1_eq, comparator_1_lt);

  // Other names for the same wires on the sheet: Ganar = out_3; Perder = out_4

  // Notes on the sheet:
  //   Entrada
  //   Salida
endmodule

module Verificar_Suma (
  input  [3:0] Carta_1,
  input  [3:0] Carta_2,
  input  [3:0] Carta_3,
  input  [3:0] Carta_4,
  input  [3:0] Carta_5,
  output out_6,
  output out_7,
  output out_8,
  output [4:0] out_9
);

  wire [4:0] adder_1_out, adder_2_out, adder_3_out, adder_4_out, bit_extender_1_out, bit_extender_2_out,
       bit_extender_3_out, bit_extender_4_out, bit_extender_5_out;

  assign bit_extender_1_out = {{1{1'b0}}, Carta_1};  // Bit_Extender bit_extender_1
  assign bit_extender_2_out = {{1{1'b0}}, Carta_2};  // Bit_Extender bit_extender_2
  assign bit_extender_3_out = {{1{1'b0}}, Carta_3};  // Bit_Extender bit_extender_3
  assign bit_extender_4_out = {{1{1'b0}}, Carta_4};  // Bit_Extender bit_extender_4
  assign bit_extender_5_out = {{1{1'b0}}, Carta_5};  // Bit_Extender bit_extender_5
  Adder #(.width(5)) adder_1 (.a(bit_extender_1_out), .b(bit_extender_2_out), .out(adder_1_out));  // open: cin, cout
  Adder #(.width(5)) adder_2 (.a(bit_extender_3_out), .b(bit_extender_4_out), .out(adder_2_out));  // open: cin, cout
  Adder #(.width(5)) adder_3 (.a(adder_2_out), .b(bit_extender_5_out), .out(adder_3_out));  // open: cin, cout
  Adder #(.width(5)) adder_4 (.a(adder_1_out), .b(adder_3_out), .out(adder_4_out));  // open: cin, cout
  Comparator #(.width(5), .mode("unsigned")) comparator_1 (
    .a(adder_4_out), .b(5'b10101), .gt(out_6), .eq(out_7), .lt(out_8));
  Multiplexer #(.width(5), .enable("false")) multiplexer_1 (
    .in0(adder_4_out), .in1({5{1'b0}}), .out(out_9), .sel(out_6));

  // Other names for the same wires on the sheet: Igual_a_21 = out_7; Mayor_a_21 = out_6; Menor_a_21 = out_8;
  //   Total[4:0] = out_9

  // Notes on the sheet:
  //   Entrada
  //   Salida
endmodule

// JUG
module \Comprobar_número_Jugador  (
  input  in_1,
  output [3:0] out_2
);

  wire and_1_out, clock_1_out, comparator_1_eq, comparator_1_gt, comparator_1_lt, comparator_2_eq,
       comparator_2_gt, comparator_2_lt, multiplexer_1_out, or_1_out, or_2_out, or_3_out;
  wire [3:0] multiplexer_2_out, random_1_out;

  Clock clock_1 (.out(clock_1_out));
  Multiplexer #(.enable("false")) multiplexer_1 (
    .in0(in_1), .in1(clock_1_out), .out(multiplexer_1_out), .sel(or_3_out));
  Random #(.width(4), .seed(8)) random_1 (.clk(multiplexer_1_out), .out(random_1_out));  // open: next, clr
  Comparator #(.width(4), .mode("unsigned")) comparator_1 (
    .a(random_1_out), .b(4'b1011), .gt(comparator_1_gt), .eq(comparator_1_eq), .lt(comparator_1_lt));
  or or_1 (or_1_out, comparator_1_eq, comparator_1_lt);
  Comparator #(.width(4), .mode("unsigned")) comparator_2 (
    .a(random_1_out), .b(4'b0000), .gt(comparator_2_gt), .eq(comparator_2_eq), .lt(comparator_2_lt));
  or or_2 (or_2_out, comparator_2_gt, comparator_2_lt);
  and and_1 (and_1_out, or_1_out, or_2_out);
  Multiplexer #(.width(4), .enable("false")) multiplexer_2 (
    .in1(random_1_out), .out(multiplexer_2_out), .sel(and_1_out));  // open: in0
  or or_3 (or_3_out, comparator_1_gt, comparator_2_eq);
  Register #(.width(4), .Select("low")) register_1 (
    .D(multiplexer_2_out), .en(and_1_out), .Q(out_2), .clk(clock_1_out));  // open: clr
endmodule

// CPU
module \Comprobar_número_CPU  (
  input  in_1,
  output [3:0] out_2
);

  wire and_1_out, clock_1_out, comparator_1_eq, comparator_1_gt, comparator_1_lt, comparator_2_eq,
       comparator_2_gt, comparator_2_lt, multiplexer_1_out, or_1_out, or_2_out, or_3_out;
  wire [3:0] multiplexer_2_out, random_1_out;

  Clock clock_1 (.out(clock_1_out));
  Multiplexer #(.enable("false")) multiplexer_1 (
    .in0(in_1), .in1(clock_1_out), .out(multiplexer_1_out), .sel(or_3_out));
  Random #(.width(4), .seed(9)) random_1 (.clk(multiplexer_1_out), .out(random_1_out));  // open: next, clr
  Comparator #(.width(4), .mode("unsigned")) comparator_1 (
    .a(random_1_out), .b(4'b1011), .gt(comparator_1_gt), .eq(comparator_1_eq), .lt(comparator_1_lt));
  or or_1 (or_1_out, comparator_1_eq, comparator_1_lt);
  Comparator #(.width(4), .mode("unsigned")) comparator_2 (
    .a(random_1_out), .b(4'b0000), .gt(comparator_2_gt), .eq(comparator_2_eq), .lt(comparator_2_lt));
  or or_2 (or_2_out, comparator_2_gt, comparator_2_lt);
  and and_1 (and_1_out, or_1_out, or_2_out);
  Multiplexer #(.width(4), .enable("false")) multiplexer_2 (
    .in1(random_1_out), .out(multiplexer_2_out), .sel(and_1_out));  // open: in0
  or or_3 (or_3_out, comparator_1_gt, comparator_2_eq);
  Register #(.width(4), .Select("low")) register_1 (
    .D(multiplexer_2_out), .en(and_1_out), .Q(out_2), .clk(clock_1_out));  // open: clr
endmodule

module Entregar_cartas (
  input  in_1,
  output [3:0] out_2,
  output [3:0] out_3,
  output [3:0] out_4,
  output [3:0] out_5
);

  wire and_1_out, and_2_out, and_3_out, and_4_out, clock_1_out, clock_2_out, clock_3_out, clock_4_out,
       comparator_1_eq, comparator_1_gt, comparator_1_lt, comparator_2_eq, comparator_2_gt, comparator_2_lt,
       comparator_3_eq, comparator_3_gt, comparator_3_lt, comparator_4_eq, comparator_4_gt, comparator_4_lt,
       comparator_5_eq, comparator_5_gt, comparator_5_lt, comparator_6_eq, comparator_6_gt, comparator_6_lt,
       comparator_7_eq, comparator_7_gt, comparator_7_lt, comparator_8_eq, comparator_8_gt, comparator_8_lt,
       multiplexer_1_out, multiplexer_2_out, multiplexer_5_out, multiplexer_6_out, or_1_out, or_2_out,
       or_3_out, or_4_out, or_5_out, or_6_out, or_7_out, or_8_out, or_9_out, or_10_out, or_11_out, or_12_out;
  wire [3:0] multiplexer_3_out, multiplexer_4_out, multiplexer_7_out, multiplexer_8_out, random_1_out,
       random_2_out, random_3_out, random_4_out;

  Clock clock_1 (.out(clock_1_out));
  Clock clock_2 (.out(clock_2_out));
  Multiplexer #(.enable("false")) multiplexer_1 (
    .in0(in_1), .in1(clock_1_out), .out(multiplexer_1_out), .sel(or_5_out));
  Multiplexer #(.enable("false")) multiplexer_2 (
    .in0(in_1), .in1(clock_2_out), .out(multiplexer_2_out), .sel(or_6_out));
  Random #(.width(4), .seed(8), .trigger("falling")) random_1 (
    .clk(multiplexer_1_out), .out(random_1_out));  // open: next, clr
  Random #(.width(4), .seed(9), .trigger("falling")) random_2 (
    .clk(multiplexer_2_out), .out(random_2_out));  // open: next, clr
  Comparator #(.width(4), .mode("unsigned")) comparator_1 (
    .a(random_1_out), .b(4'b1011), .gt(comparator_1_gt), .eq(comparator_1_eq), .lt(comparator_1_lt));
  Comparator #(.width(4), .mode("unsigned")) comparator_2 (
    .a(random_1_out), .b(4'b0000), .gt(comparator_2_gt), .eq(comparator_2_eq), .lt(comparator_2_lt));
  Comparator #(.width(4), .mode("unsigned")) comparator_3 (
    .a(random_2_out), .b(4'b1011), .gt(comparator_3_gt), .eq(comparator_3_eq), .lt(comparator_3_lt));
  or or_1 (or_1_out, comparator_1_eq, comparator_1_lt);
  or or_2 (or_2_out, comparator_2_gt, comparator_2_lt);
  or or_3 (or_3_out, comparator_3_eq, comparator_3_lt);
  Comparator #(.width(4), .mode("unsigned")) comparator_4 (
    .a(random_2_out), .b(4'b0000), .gt(comparator_4_gt), .eq(comparator_4_eq), .lt(comparator_4_lt));
  and and_1 (and_1_out, or_1_out, or_2_out);
  and and_2 (and_2_out, or_3_out, or_4_out);
  or or_4 (or_4_out, comparator_4_gt, comparator_4_lt);
  Multiplexer #(.width(4), .enable("false")) multiplexer_3 (
    .in1(random_1_out), .out(multiplexer_3_out), .sel(and_1_out));  // open: in0
  Register #(.width(4), .Select("low")) register_1 (
    .D(multiplexer_3_out), .en(and_1_out), .Q(out_2), .clk(clock_1_out));  // open: clr
  or or_5 (or_5_out, comparator_1_gt, comparator_2_eq);
  Multiplexer #(.width(4), .enable("false")) multiplexer_4 (
    .in1(random_2_out), .out(multiplexer_4_out), .sel(and_2_out));  // open: in0
  Register #(.width(4), .Select("low")) register_2 (
    .D(multiplexer_4_out), .en(and_2_out), .Q(out_3), .clk(clock_2_out));  // open: clr
  or or_6 (or_6_out, comparator_3_gt, comparator_4_eq);
  Clock clock_3 (.out(clock_3_out));
  Clock clock_4 (.out(clock_4_out));
  Multiplexer #(.enable("false")) multiplexer_5 (
    .in0(in_1), .in1(clock_3_out), .out(multiplexer_5_out), .sel(or_12_out));
  Multiplexer #(.enable("false")) multiplexer_6 (
    .in0(in_1), .in1(clock_4_out), .out(multiplexer_6_out), .sel(or_11_out));
  Random #(.width(4), .seed(6), .trigger("falling")) random_3 (
    .clk(multiplexer_5_out), .out(random_3_out));  // open: next, clr
  Random #(.width(4), .seed(10), .trigger("falling")) random_4 (
    .clk(multiplexer_6_out), .out(random_4_out));  // open: next, clr
  Comparator #(.width(4), .mode("unsigned")) comparator_5 (
    .a(random_4_out), .b(4'b1011), .gt(comparator_5_gt), .eq(comparator_5_eq), .lt(comparator_5_lt));
  Comparator #(.width(4), .mode("unsigned")) comparator_6 (
    .a(random_3_out), .b(4'b1011), .gt(comparator_6_gt), .eq(comparator_6_eq), .lt(comparator_6_lt));
  Comparator #(.width(4), .mode("unsigned")) comparator_7 (
    .a(random_3_out), .b(4'b0000), .gt(comparator_7_gt), .eq(comparator_7_eq), .lt(comparator_7_lt));
  or or_7 (or_7_out, comparator_5_eq, comparator_5_lt);
  Comparator #(.width(4), .mode("unsigned")) comparator_8 (
    .a(random_4_out), .b(4'b0000), .gt(comparator_8_gt), .eq(comparator_8_eq), .lt(comparator_8_lt));
  or or_8 (or_8_out, comparator_6_eq, comparator_6_lt);
  or or_9 (or_9_out, comparator_8_gt, comparator_8_lt);
  and and_3 (and_3_out, or_8_out, or_10_out);
  or or_10 (or_10_out, comparator_7_gt, comparator_7_lt);
  and and_4 (and_4_out, or_7_out, or_9_out);
  Multiplexer #(.width(4), .enable("false")) multiplexer_7 (
    .in1(random_3_out), .out(multiplexer_7_out), .sel(and_3_out));  // open: in0
  Multiplexer #(.width(4), .enable("false")) multiplexer_8 (
    .in1(random_4_out), .out(multiplexer_8_out), .sel(and_4_out));  // open: in0
  or or_11 (or_11_out, comparator_5_gt, comparator_8_eq);
  Register #(.width(4), .Select("low")) register_3 (
    .D(multiplexer_7_out), .en(and_3_out), .Q(out_4), .clk(clock_3_out));  // open: clr
  or or_12 (or_12_out, comparator_6_gt, comparator_7_eq);
  Register #(.width(4), .Select("low")) register_4 (
    .D(multiplexer_8_out), .en(and_4_out), .Q(out_5), .clk(clock_4_out));  // open: clr

  // Other names for the same wires on the sheet: Salida_1[3:0] = out_2; Salida_2[3:0] = out_4; Salida_3[3:0] = out_3;
  //   Salida_4[3:0] = out_5; Señal = in_1
endmodule
